# Fritzing sketch ElectrectMicrophone (saved by Fritzing 0.9.3b)

parts:
  Part4 = Bela
  Part5 = Adafruit MAX9814 Electret Microphone Amplifier [part_number="Adafruit #1713"]
  Part6 = Bela
  Part7 = Adafruit MAX9814 Electret Microphone Amplifier [part_number="Adafruit #1713"]

nets:
  N1: Part4.P9_01_GND, Part5.GND
  N2: Part4.P9_03_3.3V, Part5.VDD
  N3: Part4.Ain_00, Part5.OUTPUT
  N4: Part6.P9_01_GND, Part7.GND
  N5: Part6.P9_03_3.3V, Part7.VDD
  N6: Part6.Aout_01, Part6.In_L, Part7.OUTPUT

notes:
  Connected to bipolar audio ADC
  Connected to unipolar non-audio ADC

custom parts:
  Bela: Bela low-latency audio/sensor platform
  Adafruit MAX9814 Electret Microphone Amplifier: Add an ear to your project with this well-designed electret microphone amplifier with AGC. This fully assembled and tested board comes with a 20-20KHz electret microphone soldered on. For the amplification, we use the Maxim MAX9814, a specialty chip that is designed for amplifying electret microphones in situations where the loudness of the audio isn't predictable. This fancy microphone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
